# Fritzing sketch wiring_diagram (saved by Fritzing 0.9.3b)
breadboards: 1

parts:
  Part1 = Adafruit DC+Stepper Motor HAT [part_number="Adafruit #2348"]
  Part2 = Adafruit 4-channel I2C-safe Bi-directional Logic Level Converter [part_number="Adafruit #757"]
  D2F1 = D2F-FL Omron Snap Action Limit Switch with Level
  D2F2 = D2F-FL Omron Snap Action Limit Switch with Level
  M1 = Stepper Motor - Bipolar
  M2 = Stepper Motor - Bipolar
  U1 = RELAY-SOLIDSTATE [package=relay-s108t02]
  Encoder1 = AMT103
  Encoder2 = AMT103
  LED1 = LEDs [package=led10mm]

nets:
  N1: Part1.GPIO17, Part2.A4
  N2: Part1.GPIO18, Part2.A3
  N3: Part1.GPIO27, Part2.A2
  N4: Part1.GPIO22, Part2.A1
  N5: Part1.GPIO23, U1.+
  N6: Part1.GPIO20, D2F2.NO
  N7: Part1.GPIO21, D2F1.NO
  N8: Part1.M2A, M1.A
  N9: Part1.M2B, M1.C
  N10: Part1.M1B, M1.B
  N11: Part1.M1A, M1.D
  N12: Part1.M4A, M2.A
  N13: Part1.M4B, M2.C
  N14: Part1.M3B, M2.B
  N15: Part1.M3A, M2.D
  5V: Part1.5.0V, Part2.HV, Encoder1.5V, Encoder2.5V
  GND: Part1.GND, Part2.GND, D2F1.NC, D2F2.NC, U1.-, Encoder1.GND, Encoder2.GND
  N16: Part1.3.3V, Part2.LV
  N17: Part2.B4, Encoder1.A
  N18: Part2.B3, Encoder1.B
  N19: Part2.B2, Encoder2.A
  N20: Part2.B1, Encoder2.B
  N21: U1.T1, LED1.C

notes:
  Y Axel
  230V AC
  X-Axel
  Y-Axel

custom parts:
  Adafruit DC+Stepper Motor HAT: Let your robotic dreams come true with the new DC+Stepper Motor HAT from Adafruit. This Raspberry Pi add-on is perfect for any motion project as it can drive up to 4 DC or 2 Stepper motors with full PWM speed control. Since the Raspberry Pi does not have a lot of PWM pins, we use a fully-dedicated PWM driver chip onboard to both control motor direction and speed. This chip handles all the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
  Adafruit 4-channel I2C-safe Bi-directional Logic Level Converter: Because the Arduino (and Basic Stamp) are 5V devices, and most modern sensors, displays, flash cards and modes are 3.3V-only, many makers find that they need to perform level shifting/conversion to protect the 3.3V device from 5V. We do have some other handy level shifters in the shop, from the DIP 74LVC245 to the fancy bi-directional TXB0108. However, neither of these are happy to work with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
  D2F-FL Omron Snap Action Limit Switch with Level: Snap action switch with stainless steel lever.
  LEDs: LEDs Standard schematic elements and footprints for 5mm, 3mm, 1206, and 0603 sized LEDs. 5mm - Spark Fun Electronics SKU : COM-00529 (and others)
